// Logisim project 20240220.circ as structural Verilog: 1 circuit, main circuit main
module main (
  input  A,
  input  A_2,
  input  B,
  input  B_2,
  input  C,
  input  C_2,
  input  D,
  input  A_3,
  input  A_4,
  input  C_3,
  input  B_3,
  input  C_4,
  input  D_2,
  output Y,
  output Y_2,
  output Y_3,
  output out_17
);

  wire And_2_out, And_out, Nand_2_out, Nand_out, not_1_out, not_2_out, Or_2_out;

  and And (And_out, A, B);
  and And_2 (And_2_out, C_2, D);
  nand Nand (Nand_out, A_4, B_3);
  nand Nand_2 (Nand_2_out, C_4, D_2);
  or Or (Y_2, And_out, And_2_out);
  xor Xor (out_17, Nand_out, Nand_2_out);
  not not_1 (not_1_out, A_2);
  not not_2 (not_2_out, A_3);
  or Or_2 (Or_2_out, B_2, C);
  and And_3 (Y_3, not_2_out, C_3);
  and And_4 (Y, not_1_out, Or_2_out);

  // Notes on the sheet:
  //   Y=(A.B)+(C.D)
  //   Y=A'.(B+C)
  //   Y = f(A,B,C)
  //   Y = A'B'C+A'BC
  //   Y = A'C(B'+B)
  //   Y = A'C
endmodule
