// Logisim project 20240227-display.circ as structural Verilog: 1 circuit, main circuit main
module main (
  input  A0,
  input  B0,
  input  A1,
  input  B1,
  input  A2,
  input  B2,
  input  A3,
  input  B3,
  output Y
);

  wire XNOR_2_out, XNOR_3_out, XNOR_4_out, XNOR_out;

  xnor XNOR (XNOR_out, A0, B0);
  xnor XNOR_2 (XNOR_2_out, A1, B1);
  xnor XNOR_3 (XNOR_3_out, A2, B2);
  xnor XNOR_4 (XNOR_4_out, A0, B3);
  LED led_1 (.in(XNOR_out));
  LED led_2 (.in(XNOR_2_out));
  LED led_3 (.in(XNOR_3_out));
  LED led_4 (.in(XNOR_4_out));
  and AND (Y, XNOR_out, XNOR_2_out, XNOR_3_out, XNOR_4_out);
  LED led_5 (.in(Y));
  Hex_Digit_Display hex_digit_display_1 (.value({A0, A2, A1, A0}));  // open: dp

  assign A3 = A0;

  // Notes on the sheet:
  //   Projetar e Implementar um comparador de palavras de 4 bits
  //   A3, A2, A1, A0
  //   B3, B2, B1, B0
endmodule
