// Logisim project 20240227-material.circ as structural Verilog: 1 circuit, main circuit main
module main (
  input  A,
  input  B,
  output out_3
);

  wire AND_2_out, AND_out, NOT_2_out, NOT_out;

  not NOT (NOT_out, A);
  not NOT_2 (NOT_2_out, B);
  and AND (AND_out, NOT_out, B);
  and AND_2 (AND_2_out, A, NOT_2_out);
  or OR (out_3, AND_out, AND_2_out);

  // Notes on the sheet:
  //   A'
  //   B
  //   A
  //   B'
  //   A'B
  //   B'A
  //   X = AB' + A'B
endmodule
