// Logisim project 20240305.circ as structural Verilog: 4 circuits, main circuit A
module A (
  input  A,
  output Y
);

  nand NAND (Y, A, A);

  // Notes on the sheet:
  //   a)
  //   Para cada um dos circuitos abaixo:
  //   - Fazer a simulação no Logisim;
  //   - Montar a tabela verdade;
  //   - Achar a equação equivalente
  //   - Simplificar cada equação
  //   ____
  //   Y = A . A
  //   _
  //   = A
endmodule

module B (
  input  A,
  input  B,
  output Y
);

  wire NAND_2_out, NAND_out;

  nand NAND (NAND_out, A, A);
  nand NAND_2 (NAND_2_out, B, B);
  nand NAND_3 (Y, NAND_out, NAND_2_out);

  // Notes on the sheet:
  //   b)
  //   Para cada um dos circuitos abaixo:
  //   - Fazer a simulação no Logisim;
  //   - Montar a tabela verdade;
  //   - Achar a equação equivalente
  //   - Simplificar cada equação
  //   ____
  //    A . A
  //   ____
  //   B . B
  //   OR
  //   _____________
  //   ____
  //   ____
  //   x
  //   Y = A . A
  //   B . B
  //   _    _
  //   _    _
  //   = A + B 
  //   = A + B 
endmodule

module C (
  input  A,
  output Y
);

  nor NOR (Y, A, A);

  // Notes on the sheet:
  //   c)
  //   Para cada um dos circuitos abaixo:
  //   - Fazer a simulação no Logisim;
  //   - Montar a tabela verdade;
  //   - Achar a equação equivalente
  //   - Simplificar cada equação
  //   ____
  //   Y = A + A
  //   _
  //   = A
endmodule

module D (
  input  A,
  input  B,
  output Y
);

  wire NOR_2_out, NOR_out;

  nor NOR (NOR_out, A, A);
  nor NOR_2 (NOR_2_out, B, B);
  nor NOR_3 (Y, NOR_out, NOR_2_out);

  // Notes on the sheet:
  //   d)
  //   Para cada um dos circuitos abaixo:
  //   - Fazer a simulação no Logisim;
  //   - Montar a tabela verdade;
  //   - Achar a equação equivalente
  //   - Simplificar cada equação
  //   ____
  //    A + A
  //   ____
  //   B + B
  //   _____________
  //   ____
  //   ____
  //   Y = (A + A)
  //   (B + B)
  //   x
  //   ____
  //   _    _
  //   _    _
  //   _    _
  //   Y = (A + B)
  //   = A x B = A x B
endmodule
