// Logisim project Atividade-01-Somador.circ as structural Verilog: 1 circuit, main circuit main
module main (
  input  A,
  input  B,
  input  Cin,
  input  in_4,
  input  [3:0] in_5,
  input  [3:0] in_6,
  output SOMA,
  output [3:0] out_8,
  output out_9,
  output Cout
);

  wire AND_2_out, AND_out, XOR_out;

  xor XOR (XOR_out, A, B);
  and AND (AND_out, XOR_out, Cin);
  and AND_2 (AND_2_out, A, B);
  xor XOR_2 (SOMA, XOR_out, Cin);
  or OR (Cout, AND_out, AND_2_out);
  Adder #(.width(4)) adder_1 (.a(in_5), .b(in_6), .out(out_8), .cin(in_4), .cout(out_9));
endmodule
