// Logisim project 20240319.circ as structural Verilog: 1 circuit, main circuit main
module main (
  input  B,
  input  C,
  input  A,
  input  D,
  output out_5
);

  wire XOR_2_out, XOR_out;

  xor XOR (XOR_out, B, C);
  xor XOR_2 (XOR_2_out, A, D);
  or OR (out_5, XOR_out, XOR_2_out);

  // Notes on the sheet:
  //   Problema do Navio
endmodule
