// Logisim project somador4bits.circ as structural Verilog: 2 circuits, main circuit Somador Completo
module Somador_Completo (
  input  A0,
  input  A1,
  input  A2,
  input  A3,
  input  B0,
  input  B1,
  input  B2,
  input  B3
);

  wire adder_1_cout, adder_2_cout, adder_3_cout, adder_4_cout;
  wire [3:0] adder_1_out;

  Hex_Digit_Display hex_digit_display_1 (.value({A3, A2, A1, A0}));  // open: dp
  Hex_Digit_Display hex_digit_display_2 (.value({B3, B2, B1, B0}));  // open: dp
  Adder #(.width(1)) adder_1 (.a(A0), .b(B0), .out(adder_1_out[0]), .cin(1'b0), .cout(adder_1_cout));
  Adder #(.width(1)) adder_2 (.a(A1), .b(B1), .out(adder_1_out[1]), .cin(adder_1_cout), .cout(adder_2_cout));
  Adder #(.width(1)) adder_3 (.a(A2), .b(B2), .out(adder_1_out[2]), .cin(adder_2_cout), .cout(adder_3_cout));
  Adder #(.width(1)) adder_4 (.a(A3), .b(B3), .out(adder_1_out[3]), .cin(adder_3_cout), .cout(adder_4_cout));
  Hex_Digit_Display hex_digit_display_3 (.value(adder_1_out));  // open: dp

  // Notes on the sheet:
  //   C1 0
  //   A3 A2 A1 A0
  //   B3 B2 B1 B0
  //   S3 S2 S1 S0
  //   S out
  //   Somador Completo 4 Bits
  //   Display A
  //   Display B
  //   Display S
endmodule

module primeiratentativa (
  input  in_1,
  input  in_2,
  input  in_3,
  input  in_4,
  input  in_5,
  input  in_6,
  input  in_7,
  input  in_8,
  input  in_9,
  input  in_10,
  input  in_11,
  input  in_12
);

  wire adder_1_cout, adder_2_cout, adder_3_cout, adder_4_cout;
  wire [3:0] adder_1_out;

  Hex_Digit_Display hex_digit_display_1 (.value({in_11, in_8, in_5, in_2}));  // open: dp
  Hex_Digit_Display hex_digit_display_2 (.value({in_12, in_9, in_6, in_3}));  // open: dp
  Adder #(.width(1)) adder_1 (.a(in_2), .b(in_3), .out(adder_1_out[0]), .cin(in_1), .cout(adder_1_cout));
  // Probe on adder_1_cout
  Adder #(.width(1)) adder_2 (.a(in_5), .b(in_6), .out(adder_1_out[1]), .cin(in_4), .cout(adder_2_cout));
  // Probe on adder_2_cout
  Adder #(.width(1)) adder_3 (.a(in_8), .b(in_9), .out(adder_1_out[2]), .cin(in_7), .cout(adder_3_cout));
  // Probe on adder_3_cout
  Adder #(.width(1)) adder_4 (.a(in_11), .b(in_12), .out(adder_1_out[3]), .cin(in_10), .cout(adder_4_cout));
  // Probe on adder_4_cout
  // Probe on adder_1_out[1]
  // Probe on adder_1_out[2]
  // Probe on adder_1_out[3]
  // Probe on adder_1_out[0]
  Hex_Digit_Display hex_digit_display_3 (.value(adder_1_out));  // open: dp
endmodule
