// Logisim project Atividade-2- Somador-Subtrator-4-bits.circ as structural Verilog: 2 circuits, main circuit main
module main (
  input  A0,
  input  A1,
  input  A2,
  input  A3,
  input  B0,
  input  B1,
  input  B2,
  input  B3,
  input  in_9,
  input  in_10,
  input  in_11,
  input  in_12
);

  wire adder_1_cout, adder_1_out, adder_2_cout, adder_2_out, adder_3_cout, adder_3_out, adder_4_cout,
       adder_4_out, adder_5_cout, adder_6_cout, adder_7_cout, adder_8_cout, not_1_out, not_2_out, not_3_out,
       not_4_out;
  wire [3:0] adder_5_out;

  Hex_Digit_Display hex_digit_display_1 (.value({B3, B2, B1, B0}));  // open: dp
  Hex_Digit_Display hex_digit_display_2 (.value({A3, A2, A1, A0}));  // open: dp
  not not_1 (not_1_out, B0);
  not not_2 (not_2_out, B1);
  not not_3 (not_3_out, B2);
  not not_4 (not_4_out, B3);
  Adder #(.width(1)) adder_1 (.a(not_1_out), .b(in_9), .out(adder_1_out), .cin(1'b0), .cout(adder_1_cout));
  Adder #(.width(1)) adder_2 (.a(not_2_out), .b(in_10), .out(adder_2_out), .cin(adder_1_cout), .cout(adder_2_cout));
  Adder #(.width(1)) adder_3 (.a(not_3_out), .b(in_11), .out(adder_3_out), .cin(adder_2_cout), .cout(adder_3_cout));
  Adder #(.width(1)) adder_4 (.a(not_4_out), .b(in_12), .out(adder_4_out), .cin(adder_3_cout), .cout(adder_4_cout));
  Adder #(.width(1)) adder_5 (.a(A0), .b(adder_1_out), .out(adder_5_out[0]), .cin(1'b0), .cout(adder_5_cout));
  Adder #(.width(1)) adder_6 (.a(A1), .b(adder_2_out), .out(adder_5_out[1]), .cin(adder_5_cout), .cout(adder_6_cout));
  Adder #(.width(1)) adder_7 (.a(A2), .b(adder_3_out), .out(adder_5_out[2]), .cin(adder_6_cout), .cout(adder_7_cout));
  Adder #(.width(1)) adder_8 (.a(A3), .b(adder_4_out), .out(adder_5_out[3]), .cin(adder_7_cout), .cout(adder_8_cout));
  Hex_Digit_Display hex_digit_display_3 (.value(adder_5_out));  // open: dp
  // also tied to GND on the sheet: adder_4_cout

  // Notes on the sheet:
  //   C1 0
  //   A3 A2 A1 A0
  //   B3 B2 B1 B0
  //   S3 S2 S1 S0
  //   S out
  //   Somador Subtratror Completo 4 Bits
  //   Display A
  //   Display B
  //   Display S
endmodule

module primeiratentativa (
  input  in_1,
  input  in_2,
  input  in_3,
  input  in_4,
  input  in_5,
  input  in_6,
  input  in_7,
  input  in_8,
  input  in_9,
  input  in_10,
  input  in_11,
  input  in_12
);

  wire adder_1_cout, adder_2_cout, adder_3_cout, adder_4_cout;
  wire [3:0] adder_1_out;

  Hex_Digit_Display hex_digit_display_1 (.value({in_11, in_8, in_5, in_2}));  // open: dp
  Hex_Digit_Display hex_digit_display_2 (.value({in_12, in_9, in_6, in_3}));  // open: dp
  Adder #(.width(1)) adder_1 (.a(in_2), .b(in_3), .out(adder_1_out[0]), .cin(in_1), .cout(adder_1_cout));
  // Probe on adder_1_cout
  Adder #(.width(1)) adder_2 (.a(in_5), .b(in_6), .out(adder_1_out[1]), .cin(in_4), .cout(adder_2_cout));
  // Probe on adder_2_cout
  Adder #(.width(1)) adder_3 (.a(in_8), .b(in_9), .out(adder_1_out[2]), .cin(in_7), .cout(adder_3_cout));
  // Probe on adder_3_cout
  Adder #(.width(1)) adder_4 (.a(in_11), .b(in_12), .out(adder_1_out[3]), .cin(in_10), .cout(adder_4_cout));
  // Probe on adder_4_cout
  // Probe on adder_1_out[1]
  // Probe on adder_1_out[2]
  // Probe on adder_1_out[3]
  // Probe on adder_1_out[0]
  Hex_Digit_Display hex_digit_display_3 (.value(adder_1_out));  // open: dp
endmodule
