// Logisim project 20240416.circ as structural Verilog: 1 circuit, main circuit main
module main (
  input  A,
  input  B,
  input  C,
  input  D,
  input  A_2,
  input  B_2,
  input  C_2,
  input  D_2,
  input  E
);

  wire xor_1_out, xor_2_out, xor_3_out, xor_4_out, xor_5_out, xor_6_out, xor_7_out;

  xor xor_1 (xor_1_out, A, B);
  xor xor_2 (xor_2_out, A_2, B_2);
  xor xor_3 (xor_3_out, xor_1_out, C);
  xor xor_4 (xor_4_out, xor_2_out, C_2);
  xor xor_5 (xor_5_out, xor_3_out, D);
  xor xor_6 (xor_6_out, xor_4_out, D_2);
  LED led_1 (.in(xor_5_out));
  LED led_2 (.in(xor_7_out));
  xor xor_7 (xor_7_out, xor_6_out, E);

  // Notes on the sheet:
  //   Paridade Par
  //   A XOR B XOR C XOR D
  //   A XOR B XOR C XOR D XOR E
endmodule
