// Logisim project 240423-elevador.circ as structural Verilog: 1 circuit, main circuit main
module main (
  input  A,
  input  B,
  input  C,
  input  D,
  output out_5,
  output out_6
);

  wire and_1_out, and_2_out, not_1_out, not_2_out, not_3_out, not_4_out;

  Hex_Digit_Display hex_digit_display_1 (.value({A, B, C, D}));  // open: dp
  not not_1 (not_1_out, A);
  not not_2 (not_2_out, B);
  not not_3 (not_3_out, C);
  not not_4 (not_4_out, D);
  or or_1 (out_6, A, B);
  and and_1 (and_1_out, not_1_out, not_2_out);
  and and_2 (and_2_out, not_1_out, not_3_out, not_4_out);
  or or_2 (out_5, and_1_out, and_2_out);
  Hex_Digit_Display hex_digit_display_2 (.value({3'b000, out_5}));  // open: dp
  Hex_Digit_Display hex_digit_display_3 (.value({3'b000, out_6}));  // open: dp

  // Notes on the sheet:
  //   Elevador
  //   E1 = A'B' + A'C'D'
  //   E2 = A+B
endmodule
