// Logisim project 20240507-alarme-veiculo.circ as structural Verilog: 1 circuit, main circuit main
module main (
  input  D,
  input  P1,
  input  P2,
  input  C
);

  wire and_1_out, button_1_out, button_2_out, button_3_out, d_ff_1_q, Flip_Flop_D_2_q, Flip_Flop_D_2_qn,
       Flip_Flop_D_q, nand_1_out, or_1_out;

  Button button_1 (.out(button_1_out));
  Button button_2 (.out(button_2_out));
  D_Flip_Flop Flip_Flop_D (.clk(button_1_out), .D(D), .Q(Flip_Flop_D_q));  // open: Qn, preset, en, reset
  D_Flip_Flop Flip_Flop_D_2 (
    .clk(button_2_out), .D(Flip_Flop_D_2_qn), .Q(Flip_Flop_D_2_q), .Qn(Flip_Flop_D_2_qn));  // open: preset, en, reset
  nand nand_1 (nand_1_out, P1, P2, C);
  LED led_1 (.in(Flip_Flop_D_q));
  LED Porta_Fechada (.in(nand_1_out));
  or or_1 (or_1_out, Flip_Flop_D_2_qn, button_3_out);
  D_Flip_Flop d_ff_1 (.clk(nand_1_out), .D(1'b0), .Q(d_ff_1_q), .reset(or_1_out));  // open: Qn, preset, en
  Button button_3 (.out(button_3_out));
  and and_1 (and_1_out, Flip_Flop_D_2_q, d_ff_1_q);
  LED led_2 (.in(and_1_out));

  // Notes on the sheet:
  //   Alarme de Veículo
  //   Circuito Sequencial
endmodule
