// Logisim project 20240507-registrador-com-deslocamento.circ as structural Verilog: 1 circuit, main circuit main
module main (
  input  in_1,
  input  in_2,
  input  in_3,
  input  in_4,
  input  in_5,
  input  in_6,
  input  in_7,
  input  in_8,
  input  Carga__Load,
  input  in_10,
  input  in_11,
  input  Clear__Limpa,
  output out_13
);

  wire button_1_out;
  wire [3:0] shift_register_1_q3, shift_register_1_q7;

  Button button_1 (.out(button_1_out));
  Shift_Register shift_register_1 (
    .shift(in_10), .in(in_11), .clk(button_1_out), .out(out_13), .load(Carga__Load), .clr(Clear__Limpa),
    .d0(in_1), .q0(shift_register_1_q3[3]), .d1(in_2), .q1(shift_register_1_q3[2]), .d2(in_3),
    .q2(shift_register_1_q3[1]), .d3(in_4), .q3(shift_register_1_q3[0]), .d4(in_5),
    .q4(shift_register_1_q7[3]), .d5(in_6), .q5(shift_register_1_q7[2]), .d6(in_7),
    .q6(shift_register_1_q7[1]), .d7(in_8), .q7(shift_register_1_q7[0]));
  Hex_Digit_Display hex_digit_display_1 (.value(shift_register_1_q3));  // open: dp
  Hex_Digit_Display hex_digit_display_2 (.value(shift_register_1_q7));  // open: dp

  // Notes on the sheet:
  //   Habilita Deslocamento
  //   Valor (1° Estágio)
  //   Clock (Gatilho)
  //   Registrador de Deslocamento de 08 Bits
  //   Entradas (8 bits)
  //   Saídas (8 bits)
  //   Valor (Último Estágio)
endmodule
