// Logisim project 20240507-registrador.circ as structural Verilog: 1 circuit, main circuit main
module main (
  input  in_1,
  input  in_2,
  input  in_3,
  input  in_4,
  input  in_5,
  input  in_6,
  input  in_7,
  input  in_8
);

  wire button_1_out;
  wire [7:0] register_1_q;

  Register register_1 (
    .D({in_1, in_2, in_3, in_4, in_5, in_6, in_7, in_8}), .Q(register_1_q), .clk(button_1_out));  // open: en, clr
  Button button_1 (.out(button_1_out));
  Hex_Digit_Display hex_digit_display_1 (.value(register_1_q[7:4]));  // open: dp
  Hex_Digit_Display hex_digit_display_2 (.value(register_1_q[3:0]));  // open: dp

  // Notes on the sheet:
  //   Registrador de 08 Bits
  //   Entradas (8 bits)
  //   Reg 8 bits
  //   Saídas (8 bits)
  //   Clock (Gatilho)
endmodule
