// Logisim project 20240521 - Atividade 3.circ as structural Verilog: 2 circuits, main circuit main
module main (
  input  in_1,
  input  in_2,
  output out_3,
  output out_4,
  output out_5
);

  wire and_1_out, and_2_out, clock_1_out, j_k_ff_1_qn;

  Clock clock_1 (.out(clock_1_out));
  J_K_Flip_Flop #(.trigger("falling")) j_k_ff_1 (
    .J(in_1), .clk(clock_1_out), .K(j_k_ff_1_qn), .Q(out_5), .Qn(j_k_ff_1_qn));  // open: preset, en, reset
  J_K_Flip_Flop #(.trigger("falling")) j_k_ff_2 (
    .J(out_5), .clk(clock_1_out), .K(in_2), .Q(out_4));  // open: Qn, preset, en, reset
  and and_1 (and_1_out, out_4, j_k_ff_1_qn);
  and and_2 (and_2_out, out_5, out_4);
  J_K_Flip_Flop #(.trigger("falling")) j_k_ff_3 (
    .J(and_2_out), .clk(clock_1_out), .K(and_1_out), .Q(out_3));  // open: Qn, preset, en, reset

  // Notes on the sheet:
  //   C
  //   B
  //   A
endmodule

module redesign (
  input  in_1,
  input  in_2,
  output out_3,
  output out_4,
  output out_5
);

  wire clock_1_out, j_k_ff_1_qn, JA___BC_out, or_1_out;

  Clock clock_1 (.out(clock_1_out));
  J_K_Flip_Flop #(.trigger("falling")) j_k_ff_1 (
    .J(in_1), .clk(clock_1_out), .K(j_k_ff_1_qn), .Q(out_5), .Qn(j_k_ff_1_qn));  // open: preset, en, reset
  J_K_Flip_Flop #(.trigger("falling")) j_k_ff_2 (
    .J(out_5), .clk(clock_1_out), .K(in_2), .Q(out_4));  // open: Qn, preset, en, reset
  and JA___BC (JA___BC_out, out_5, out_4);
  or or_1 (or_1_out, out_4, j_k_ff_1_qn);
  J_K_Flip_Flop #(.trigger("falling")) j_k_ff_3 (
    .J(JA___BC_out), .clk(clock_1_out), .K(or_1_out), .Q(out_3));  // open: Qn, preset, en, reset

  // Notes on the sheet:
  //   Atividade 3 - Contador Síncrono de números ímpares de 1 a 7 
  //   C
  //   B
  //   A
endmodule
