// Logisim project 4bits.circ as structural Verilog: 1 circuit, main circuit main
module main (
  output A,
  output B,
  output C,
  output D
);

  wire A_qn, and_1_out, and_2_out, and_3_out, and_4_out, clock_1_out, D_qn;

  Clock clock_1 (.out(clock_1_out));
  J_K_Flip_Flop #(.trigger("falling")) u_D (
    .J(1'b1), .clk(clock_1_out), .K(1'b1), .Q(D), .Qn(D_qn));  // open: preset, en, reset
  and and_1 (and_1_out, D, A_qn);
  J_K_Flip_Flop #(.trigger("falling")) u_C (
    .J(and_1_out), .clk(clock_1_out), .K(D), .Q(C));  // open: Qn, preset, en, reset
  and and_2 (and_2_out, C, D_qn);
  and and_3 (and_3_out, C, D);
  J_K_Flip_Flop #(.trigger("falling")) u_B (
    .J(and_2_out), .clk(clock_1_out), .K(and_3_out), .Q(B));  // open: Qn, preset, en, reset
  and and_4 (and_4_out, D, C, B);
  J_K_Flip_Flop #(.trigger("falling")) u_A (
    .J(and_4_out), .clk(clock_1_out), .K(D), .Q(A), .Qn(A_qn));  // open: preset, en, reset
endmodule
