// Logisim project cronometrov2.circ as structural Verilog: 5 circuits, main circuit main
module main (
  input  in_1,
  input  in_2,
  input  in_3,
  input  in_4
);

  wire and_1_out, and_2_out, and_3_out, and_4_out, and_5_out, and_6_out, and_7_out, and_8_out, and_9_out,
       and_10_out, clock_1_out;
  wire [1:0] _0_2_out_4;
  wire [2:0] _0___5_2_out_5, _0___5_out_5;
  wire [3:0] _0_9_2_out_6, _0_9_3_out_6, _0_9_out_6;

  and and_1 (and_1_out, _0_9_out_6[3], _0_9_out_6[0]);
  jk2 _0_2 (.Clock(and_1_out), .ZERAR(and_3_out), .out_3(_0_2_out_4[1]), .out_4(_0_2_out_4[0]));
  Hex_Digit_Display hex_digit_display_1 (.value({{2{in_3}}, _0_2_out_4}));  // open: dp
  and and_2 (and_2_out, _0_2_out_4[1], _0_9_out_6[1], _0_9_out_6[0]);
  jk9 _0_9 (
    .Clock(and_4_out), .ZERAR(and_3_out), .out_3(_0_9_out_6[3]), .out_4(_0_9_out_6[2]),
    .out_5(_0_9_out_6[1]), .out_6(_0_9_out_6[0]));
  and and_3 (and_3_out, and_2_out, and_5_out, and_7_out);
  Hex_Digit_Display hex_digit_display_2 (.value(_0_9_out_6));  // open: dp
  jk5 _0___5 (
    .Clock(and_6_out), .ZERAR(and_3_out), .out_3(_0___5_out_5[2]), .out_4(_0___5_out_5[1]),
    .out_5(_0___5_out_5[0]));
  and and_4 (and_4_out, _0___5_out_5[2], _0___5_out_5[0]);
  and and_5 (and_5_out, _0___5_out_5[2], _0___5_out_5[0]);
  Hex_Digit_Display hex_digit_display_3 (.value({in_2, _0___5_out_5}));  // open: dp
  jk9 _0_9_2 (
    .Clock(and_8_out), .ZERAR(and_3_out), .out_3(_0_9_2_out_6[3]), .out_4(_0_9_2_out_6[2]),
    .out_5(_0_9_2_out_6[1]), .out_6(_0_9_2_out_6[0]));
  and and_6 (and_6_out, _0_9_2_out_6[3], _0_9_2_out_6[0]);
  and and_7 (and_7_out, _0_9_2_out_6[3], _0_9_2_out_6[0]);
  Hex_Digit_Display hex_digit_display_4 (.value(_0_9_2_out_6));  // open: dp
  jk5 _0___5_2 (
    .Clock(and_10_out), .ZERAR(and_3_out), .out_3(_0___5_2_out_5[2]), .out_4(_0___5_2_out_5[1]),
    .out_5(_0___5_2_out_5[0]));
  and and_8 (and_8_out, _0___5_2_out_5[2], _0___5_2_out_5[0]);
  Clock clock_1 (.out(clock_1_out));
  Hex_Digit_Display hex_digit_display_5 (.value({in_1, _0___5_2_out_5}));  // open: dp
  and and_9 (and_9_out, clock_1_out, in_4);
  jk9 _0_9_3 (
    .Clock(and_9_out), .ZERAR(and_3_out), .out_3(_0_9_3_out_6[3]), .out_4(_0_9_3_out_6[2]),
    .out_5(_0_9_3_out_6[1]), .out_6(_0_9_3_out_6[0]));
  and and_10 (and_10_out, _0_9_3_out_6[3], _0_9_3_out_6[0]);
  Hex_Digit_Display hex_digit_display_6 (.value(_0_9_3_out_6));  // open: dp

  // Notes on the sheet:
  //   BOTAO START/STOP
endmodule

module jk9 (
  input  Clock,
  input  ZERAR,
  output out_3,
  output out_4,
  output out_5,
  output out_6
);

  wire A_qn, and_1_out, and_2_out, and_3_out;

  J_K_Flip_Flop #(.trigger("falling")) D (
    .J(1'b1), .clk(Clock), .K(1'b1), .Q(out_6), .reset(ZERAR));  // open: Qn, preset, en
  and and_1 (and_1_out, out_6, A_qn);
  J_K_Flip_Flop #(.trigger("falling")) C (
    .J(and_1_out), .clk(Clock), .K(out_6), .Q(out_5), .reset(ZERAR));  // open: Qn, preset, en
  and and_2 (and_2_out, out_6, out_5);
  J_K_Flip_Flop #(.trigger("falling")) B (
    .J(and_2_out), .clk(Clock), .K(and_2_out), .Q(out_4), .reset(ZERAR));  // open: Qn, preset, en
  and and_3 (and_3_out, out_6, out_5, out_4);
  J_K_Flip_Flop #(.trigger("falling")) A (
    .J(and_3_out), .clk(Clock), .K(out_6), .Q(out_3), .Qn(A_qn), .reset(ZERAR));  // open: preset, en
endmodule

module jk5 (
  input  Clock,
  input  ZERAR,
  output out_3,
  output out_4,
  output out_5
);

  wire A_qn, and_1_out, and_2_out;

  J_K_Flip_Flop #(.trigger("falling")) C (
    .J(1'b1), .clk(Clock), .K(1'b1), .Q(out_5), .reset(ZERAR));  // open: Qn, preset, en
  and and_1 (and_1_out, A_qn, out_5);
  J_K_Flip_Flop #(.trigger("falling")) B (
    .J(and_1_out), .clk(Clock), .K(out_5), .Q(out_4), .reset(ZERAR));  // open: Qn, preset, en
  and and_2 (and_2_out, out_5, out_4);
  J_K_Flip_Flop #(.trigger("falling")) A (
    .J(and_2_out), .clk(Clock), .K(out_5), .Q(out_3), .Qn(A_qn), .reset(ZERAR));  // open: preset, en
endmodule

module jk3 (
  output out_1,
  output out_2
);

  wire clock_1_out;

  Clock clock_1 (.out(clock_1_out));
  J_K_Flip_Flop #(.trigger("falling")) B (
    .J(1'b1), .clk(clock_1_out), .K(1'b1), .Q(out_2));  // open: Qn, preset, en, reset
  J_K_Flip_Flop #(.trigger("falling")) A (
    .J(out_2), .clk(clock_1_out), .K(out_2), .Q(out_1));  // open: Qn, preset, en, reset
endmodule

module jk2 (
  input  Clock,
  input  ZERAR,
  output out_3,
  output out_4
);

  wire A_qn;

  J_K_Flip_Flop #(.trigger("falling")) B (
    .J(A_qn), .clk(Clock), .K(1'b1), .Q(out_4), .reset(ZERAR));  // open: Qn, preset, en
  J_K_Flip_Flop #(.trigger("falling")) A (
    .J(out_4), .clk(Clock), .K(1'b1), .Q(out_3), .Qn(A_qn), .reset(ZERAR));  // open: preset, en
endmodule
