// Logisim project cronometroV6.circ as structural Verilog: 4 circuits, main circuit main
module main (
  input  in_1,
  input  in_2,
  input  in_3,
  input  in_4,
  input  in_5
);

  wire and_1_out, and_2_out, and_3_out, and_4_out, and_5_out, and_6_out, and_7_out, button_1_out,
       clock_1_out, multiplexer_1_out, multiplexer_2_out, multiplexer_3_out, multiplexer_4_out,
       multiplexer_5_out, nor_1_out, nor_2_out, nor_3_out, nor_4_out, nor_5_out, or_1_out;
  wire [1:0] jk2_1_b;
  wire [2:0] _0_5_out_6, _0___5_out_6;
  wire [3:0] _0_9_2_d, _0_9_3_d, _0_9_d;

  and and_1 (and_1_out, _0_9_d[3], _0_9_d[0]);
  Multiplexer multiplexer_1 (.in0(and_1_out), .in1(nor_1_out), .out(multiplexer_1_out), .sel(in_5));  // open: en
  nor nor_1 (nor_1_out, _0_9_d[3], _0_9_d[0], _0_9_d[2], _0_9_d[1]);
  jk2 jk2_1 (
    .Clock(multiplexer_1_out), .ZERAR(or_1_out), ._0___CRESCENTE_1___DECRESCENTE(in_5), .A(jk2_1_b[1]),
    .B(jk2_1_b[0]));
  Button button_1 (.out(button_1_out));
  jk9 _0_9 (
    .Clock(multiplexer_2_out), .ZERAR(or_1_out), ._0___CRECESCENTE_1__DECRESCENTE(in_5), .A(_0_9_d[3]),
    .B(_0_9_d[2]), .C(_0_9_d[1]), .D(_0_9_d[0]));
  and and_2 (and_2_out, jk2_1_b[1], _0_9_d[2]);
  or or_1 (or_1_out, button_1_out, and_2_out);
  Multiplexer multiplexer_2 (.in0(and_3_out), .in1(nor_2_out), .out(multiplexer_2_out), .sel(in_5));  // open: en
  Hex_Digit_Display hex_digit_display_1 (.value({{2{in_3}}, jk2_1_b}));  // open: dp
  Hex_Digit_Display hex_digit_display_2 (.value(_0_9_d));  // open: dp
  jk5 _0_5 (
    .CLOCK(multiplexer_3_out), .ZERAR(or_1_out), ._0___CRESCENTE_1___DECRESCENTE(in_5), .A(_0_5_out_6[2]),
    .B(_0_5_out_6[1]), .out_6(_0_5_out_6[0]));
  and and_3 (and_3_out, _0_5_out_6[2], _0_5_out_6[0]);
  nor nor_2 (nor_2_out, _0_5_out_6[0], _0_5_out_6[1], _0_5_out_6[2]);
  Hex_Digit_Display hex_digit_display_3 (.value({in_1, _0_5_out_6}));  // open: dp
  Hex_Digit_Display hex_digit_display_4 (.value(_0_9_2_d));  // open: dp
  Multiplexer multiplexer_3 (.in0(and_4_out), .in1(nor_3_out), .out(multiplexer_3_out), .sel(in_5));  // open: en
  Hex_Digit_Display hex_digit_display_5 (.value(_0_9_3_d));  // open: dp
  Hex_Digit_Display hex_digit_display_6 (.value({in_2, _0___5_out_6}));  // open: dp
  jk9 _0_9_2 (
    .Clock(multiplexer_4_out), .ZERAR(or_1_out), ._0___CRECESCENTE_1__DECRESCENTE(in_5), .A(_0_9_2_d[3]),
    .B(_0_9_2_d[2]), .C(_0_9_2_d[1]), .D(_0_9_2_d[0]));
  and and_4 (and_4_out, _0_9_2_d[3], _0_9_2_d[0]);
  nor nor_3 (nor_3_out, _0_9_2_d[0], _0_9_2_d[1], _0_9_2_d[2], _0_9_2_d[3]);
  Multiplexer multiplexer_4 (.in0(and_5_out), .in1(nor_4_out), .out(multiplexer_4_out), .sel(in_5));  // open: en
  jk5 _0___5 (
    .CLOCK(multiplexer_5_out), .ZERAR(or_1_out), ._0___CRESCENTE_1___DECRESCENTE(in_5), .A(_0___5_out_6[2]),
    .B(_0___5_out_6[1]), .out_6(_0___5_out_6[0]));
  and and_5 (and_5_out, _0___5_out_6[2], _0___5_out_6[0]);
  nor nor_4 (nor_4_out, _0___5_out_6[0], _0___5_out_6[1], _0___5_out_6[2]);
  Clock clock_1 (.out(clock_1_out));
  and and_6 (and_6_out, clock_1_out, in_4);
  jk9 _0_9_3 (
    .Clock(and_6_out), .ZERAR(or_1_out), ._0___CRECESCENTE_1__DECRESCENTE(in_5), .A(_0_9_3_d[3]),
    .B(_0_9_3_d[2]), .C(_0_9_3_d[1]), .D(_0_9_3_d[0]));
  and and_7 (and_7_out, _0_9_3_d[3], _0_9_3_d[0]);
  Multiplexer multiplexer_5 (.in0(and_7_out), .in1(nor_5_out), .out(multiplexer_5_out), .sel(in_5));  // open: en
  nor nor_5 (nor_5_out, _0_9_3_d[0], _0_9_3_d[1], _0_9_3_d[2], _0_9_3_d[3]);

  // Notes on the sheet:
  //   BOTÃO ZERAR
  //   BOTAO START/STOP
endmodule

module jk9 (
  input  Clock,
  input  ZERAR,
  input  _0___CRECESCENTE_1__DECRESCENTE,
  output A,
  output B,
  output C,
  output D
);

  wire A_qn, and_1_out, and_2_out, and_3_out, and_4_out, and_5_out, and_6_out, and_7_out, B_qn, C_qn, D_qn,
       multiplexer_1_out, multiplexer_2_out, multiplexer_3_out, multiplexer_4_out, multiplexer_5_out,
       multiplexer_6_out, or_1_out;

  J_K_Flip_Flop #(.trigger("falling")) u_D (
    .J(1'b1), .clk(Clock), .K(1'b1), .Q(D), .Qn(D_qn), .reset(ZERAR));  // open: preset, en
  or or_1 (or_1_out, and_3_out, and_2_out);
  and and_1 (and_1_out, A_qn, D);
  Multiplexer multiplexer_1 (
    .in0(and_1_out), .in1(or_1_out), .out(multiplexer_1_out), .sel(_0___CRECESCENTE_1__DECRESCENTE));  // open: en
  and and_2 (and_2_out, D_qn, C_qn, B);
  Multiplexer multiplexer_2 (
    .in0(D), .in1(D_qn), .out(multiplexer_2_out), .sel(_0___CRECESCENTE_1__DECRESCENTE));  // open: en
  and and_3 (and_3_out, D_qn, A);
  J_K_Flip_Flop #(.trigger("falling")) u_C (
    .J(multiplexer_1_out), .clk(Clock), .K(multiplexer_2_out), .Q(C), .Qn(C_qn), .reset(ZERAR));  // open: preset, en
  and and_4 (and_4_out, C_qn, D_qn);
  and and_5 (and_5_out, D, C);
  Multiplexer multiplexer_3 (
    .in0(and_5_out), .in1(and_4_out), .out(multiplexer_3_out), .sel(_0___CRECESCENTE_1__DECRESCENTE));  // open: en
  Multiplexer multiplexer_4 (
    .in0(and_5_out), .in1(and_3_out), .out(multiplexer_4_out), .sel(_0___CRECESCENTE_1__DECRESCENTE));  // open: en
  J_K_Flip_Flop #(.trigger("falling")) u_B (
    .J(multiplexer_4_out), .clk(Clock), .K(multiplexer_3_out), .Q(B), .Qn(B_qn), .reset(ZERAR));  // open: preset, en
  and and_6 (and_6_out, B_qn, C_qn, D_qn);
  and and_7 (and_7_out, D, C, B);
  Multiplexer multiplexer_5 (
    .in0(and_7_out), .in1(and_6_out), .out(multiplexer_5_out), .sel(_0___CRECESCENTE_1__DECRESCENTE));  // open: en
  Multiplexer multiplexer_6 (
    .in0(D), .in1(D_qn), .out(multiplexer_6_out), .sel(_0___CRECESCENTE_1__DECRESCENTE));  // open: en
  J_K_Flip_Flop #(.trigger("falling")) u_A (
    .J(multiplexer_5_out), .clk(Clock), .K(multiplexer_6_out), .Q(A), .Qn(A_qn), .reset(ZERAR));  // open: preset, en
endmodule

module jk5 (
  input  CLOCK,
  input  ZERAR,
  input  _0___CRESCENTE_1___DECRESCENTE,
  output A,
  output B,
  output out_6
);

  wire A_qn, and_1_out, and_2_out, and_3_out, and_4_out, B_qn, C_qn, multiplexer_1_out, multiplexer_2_out,
       multiplexer_3_out, not_1_out;

  J_K_Flip_Flop #(.trigger("falling")) C (
    .J(1'b1), .clk(CLOCK), .K(1'b1), .Q(out_6), .Qn(C_qn), .reset(ZERAR));  // open: preset, en
  and and_1 (and_1_out, A_qn, out_6);
  and and_2 (and_2_out, A, C_qn);
  Multiplexer multiplexer_1 (
    .in0(and_1_out), .in1(and_2_out), .out(multiplexer_1_out), .sel(_0___CRESCENTE_1___DECRESCENTE));  // open: en
  and and_3 (and_3_out, out_6, B);
  and and_4 (and_4_out, C_qn, B_qn);
  J_K_Flip_Flop #(.trigger("falling")) u_B (
    .J(multiplexer_1_out), .clk(CLOCK), .K(multiplexer_3_out), .Q(B), .Qn(B_qn), .reset(ZERAR));  // open: preset, en
  not not_1 (not_1_out, C_qn);
  Multiplexer multiplexer_2 (
    .in0(and_3_out), .in1(and_4_out), .out(multiplexer_2_out), .sel(_0___CRESCENTE_1___DECRESCENTE));  // open: en
  Multiplexer multiplexer_3 (
    .in0(not_1_out), .in1(C_qn), .out(multiplexer_3_out), .sel(_0___CRESCENTE_1___DECRESCENTE));  // open: en
  J_K_Flip_Flop #(.trigger("falling")) u_A (
    .J(multiplexer_2_out), .clk(CLOCK), .K(multiplexer_3_out), .Q(A), .Qn(A_qn), .reset(ZERAR));  // open: preset, en
endmodule

module jk2 (
  input  Clock,
  input  ZERAR,
  input  _0___CRESCENTE_1___DECRESCENTE,
  output A,
  output B
);

  wire A_qn, B_qn, multiplexer_1_out, multiplexer_2_out;

  Multiplexer multiplexer_1 (
    .in0(A_qn), .in1(A), .out(multiplexer_1_out), .sel(_0___CRESCENTE_1___DECRESCENTE));  // open: en
  J_K_Flip_Flop #(.trigger("falling")) u_B (
    .J(multiplexer_1_out), .clk(Clock), .K(1'b1), .Q(B), .Qn(B_qn), .reset(ZERAR));  // open: preset, en
  Multiplexer multiplexer_2 (
    .in0(B), .in1(B_qn), .out(multiplexer_2_out), .sel(_0___CRESCENTE_1___DECRESCENTE));  // open: en
  J_K_Flip_Flop #(.trigger("falling")) u_A (
    .J(multiplexer_2_out), .clk(Clock), .K(1'b1), .Q(A), .Qn(A_qn), .reset(ZERAR));  // open: preset, en
endmodule
